// Logisim project 1607077_1607073_project .circ as structural Verilog: 16 circuits, main circuit main
module main (
  input  clear,
  output [3:0] High,
  output [3:0] low,
  output out_4,
  output out_5,
  output out_6,
  output out_7,
  output out_8,
  output out_9,
  output out_10,
  output out_11
);

  wire clk_out, controlled_buffer_1_out, controlled_buffer_4_out, controller_1_cp, controller_1_ea,
       controller_1_ep, controller_1_eu, controller_1_hlt, controller_1_nce, controller_1_nei,
       controller_1_nla, controller_1_nlb, controller_1_nli, controller_1_nlm, controller_1_nlo,
       controller_1_su, not_1_out, not_2_out, not_3_out, not_4_out, not_5_out, not_6_out, not_7_out,
       not_8_out;
  wire [3:0] counter_1_q, Instrac_Reg_high, Instrac_Reg_low, MAR_x0_2;
  wire [7:0] A_output, B_output;

  assign controlled_buffer_1_out = controller_1_cp ? controlled_buffer_4_out : 1'bz;  // Controlled_Buffer controlled_buffer_1
  Counter #(.width(4), .max('hf)) counter_1 (
    .Q(counter_1_q), .clk(controlled_buffer_1_out), .clr(clear));  // open: load, D, count, carry
  _4_bit__buffer_register MAR (
    .load(not_1_out), .CLK(controlled_buffer_4_out), .CLR(clear), .X0(low[0]), .X1(low[1]), .X2(low[2]),
    .X3(low[3]), .x0_2(MAR_x0_2[0]), .x1_2(MAR_x0_2[1]), .x2_2(MAR_x0_2[2]), .x3_2(MAR_x0_2[3]));
  not not_1 (not_1_out, controller_1_nlm);
  not not_2 (not_2_out, controller_1_nce);
  not not_3 (not_3_out, controller_1_nli);
  controller controller_1 (
    .clear(clear), .CLK(controlled_buffer_4_out), .CP(controller_1_cp), .EP(controller_1_ep),
    .I4(Instrac_Reg_high[0]), .I5(Instrac_Reg_high[1]), .I6(Instrac_Reg_high[2]), .I7(Instrac_Reg_high[3]),
    .HLT(controller_1_hlt), .nLM(controller_1_nlm), .nCE(controller_1_nce), .nEI(controller_1_nei),
    .nLA(controller_1_nla), .EA(controller_1_ea), .SU(controller_1_su), .EU(controller_1_eu),
    .nLB(controller_1_nlb), .nLO(controller_1_nlo), .nLI(controller_1_nli));
  assign low = controller_1_ep ? counter_1_q : 4'bz;  // Controlled_Buffer controlled_buffer_2
  RAM #(.addrWidth(4)) ram_1 (.addr(MAR_x0_2), .data({High, low}), .ld(not_2_out));  // open: sel, clk, clr
  _8_bit_register Instrac_Reg (
    .load(not_3_out), .CLK(controlled_buffer_4_out), .CLR(clear), .HighI(High), .LowI(low),
    .Low(Instrac_Reg_low), .High(Instrac_Reg_high));
  assign low = not_4_out ? Instrac_Reg_low : 4'bz;  // Controlled_Buffer controlled_buffer_3
  not not_4 (not_4_out, controller_1_nei);
  not not_5 (not_5_out, controller_1_hlt);
  Clock clk (.out(clk_out));
  assign controlled_buffer_4_out = not_5_out ? clk_out : 1'bz;  // Controlled_Buffer controlled_buffer_4
  assign {High, low} = controller_1_ea ? A_output : 8'bz;  // Controlled_Buffer controlled_buffer_5
  not not_6 (not_6_out, controller_1_nla);
  not not_7 (not_7_out, controller_1_nlb);
  REGISTER_8_BIT A (
    .Input({High, low}), .Load(not_6_out), .clock_pulse(controlled_buffer_4_out), .Clear(clear),
    .Output(A_output));
  ALU ALU (.A(A_output), .B(B_output), .Su(controller_1_su), .Eu(controller_1_eu), .Output({High, low}));
  REGISTER_8_BIT B (
    .Input({High, low}), .Load(not_7_out), .clock_pulse(controlled_buffer_4_out), .Clear(clear),
    .Output(B_output));
  REGISTER_8_BIT \output  (
    .Input({High, low}), .Load(not_8_out), .clock_pulse(controlled_buffer_4_out), .Clear(clear),
    .Output({out_4, out_5, out_6, out_7, out_8, out_9, out_10, out_11}));
  not not_8 (not_8_out, controller_1_nlo);
  Hex_Digit_Display hex_digit_display_1 (.value({out_4, out_5, out_6, out_7}));  // open: dp
  Hex_Digit_Display hex_digit_display_2 (.value({out_8, out_9, out_10, out_11}));  // open: dp

  // Notes on the sheet:
  //   1607077
  //   1607073
endmodule

module _4_bit__buffer_register (
  input  X0,
  input  X1,
  input  X2,
  input  X3,
  input  load,
  input  CLK,
  input  CLR,
  output x0_2,
  output x1_2,
  output x2_2,
  output x3_2
);

  wire and_1_out, and_2_out, and_3_out, and_4_out, and_5_out, and_6_out, and_7_out, and_8_out, d_ff_1_q,
       d_ff_2_q, d_ff_3_q, d_ff_4_q, not_1_out, or_1_out, or_2_out, or_3_out, or_4_out;

  not not_1 (not_1_out, load);
  and and_1 (and_1_out, load, X0);
  or or_1 (or_1_out, and_1_out, and_2_out);
  and and_2 (and_2_out, not_1_out, d_ff_1_q);
  D_Flip_Flop d_ff_1 (.clk(CLK), .D(or_1_out), .Q(d_ff_1_q), .reset(CLR));  // open: Qn, preset, en
  assign x0_2 = 1'b1 ? d_ff_1_q : 1'bz;  // Controlled_Buffer controlled_buffer_1
  and and_3 (and_3_out, load, X1);
  or or_2 (or_2_out, and_3_out, and_4_out);
  and and_4 (and_4_out, not_1_out, d_ff_2_q);
  D_Flip_Flop d_ff_2 (.clk(CLK), .D(or_2_out), .Q(d_ff_2_q), .reset(CLR));  // open: Qn, preset, en
  assign x1_2 = 1'b1 ? d_ff_2_q : 1'bz;  // Controlled_Buffer controlled_buffer_2
  and and_5 (and_5_out, load, X2);
  or or_3 (or_3_out, and_5_out, and_6_out);
  D_Flip_Flop d_ff_3 (.clk(CLK), .D(or_3_out), .Q(d_ff_3_q), .reset(CLR));  // open: Qn, preset, en
  and and_6 (and_6_out, not_1_out, d_ff_3_q);
  assign x2_2 = 1'b1 ? d_ff_3_q : 1'bz;  // Controlled_Buffer controlled_buffer_3
  and and_7 (and_7_out, load, X3);
  or or_4 (or_4_out, and_7_out, and_8_out);
  and and_8 (and_8_out, not_1_out, d_ff_4_q);
  D_Flip_Flop d_ff_4 (.clk(CLK), .D(or_4_out), .Q(d_ff_4_q), .reset(CLR));  // open: Qn, preset, en
  assign x3_2 = 1'b1 ? d_ff_4_q : 1'bz;  // Controlled_Buffer controlled_buffer_4

  // Notes on the sheet:
  //   1607077
endmodule

module _8_bit_register (
  input  [3:0] LowI,
  input  load,
  input  CLK,
  input  CLR,
  input  [3:0] HighI,
  output [3:0] Low,
  output [3:0] High
);

  _4_bit__buffer_register u_4_bit_buffer_register_1 (
    .load(load), .CLK(CLK), .CLR(CLR), .X0(HighI[0]), .X1(HighI[1]), .X2(HighI[2]), .X3(HighI[3]),
    .x0_2(High[0]), .x1_2(High[1]), .x2_2(High[2]), .x3_2(High[3]));
  _4_bit__buffer_register u_4_bit_buffer_register_2 (
    .load(load), .CLK(CLK), .CLR(CLR), .X0(LowI[0]), .X1(LowI[1]), .X2(LowI[2]), .X3(LowI[3]), .x0_2(Low[0]),
    .x1_2(Low[1]), .x2_2(Low[2]), .x3_2(Low[3]));

  // Notes on the sheet:
  //   1607077
  //   1607077
endmodule

module program_counter (
  input  Count,
  input  Clock_pulse,
  input  Clear,
  input  Enable,
  output [3:0] Output
);

  wire j_k_ff_1_q, j_k_ff_2_q, j_k_ff_3_q, j_k_ff_4_q, not_1_out, not_2_out, not_3_out, not_4_out;

  not not_1 (not_1_out, Clock_pulse);
  J_K_Flip_Flop j_k_ff_1 (
    .J(Count), .clk(not_1_out), .K(Count), .Q(j_k_ff_1_q), .reset(Clear));  // open: Qn, preset, en
  assign Output[0] = Enable ? j_k_ff_1_q : 1'bz;  // Controlled_Buffer controlled_buffer_1
  not not_2 (not_2_out, j_k_ff_1_q);
  J_K_Flip_Flop j_k_ff_2 (
    .J(Count), .clk(not_2_out), .K(Count), .Q(j_k_ff_2_q), .reset(Clear));  // open: Qn, preset, en
  assign Output[1] = Enable ? j_k_ff_2_q : 1'bz;  // Controlled_Buffer controlled_buffer_2
  not not_3 (not_3_out, j_k_ff_2_q);
  J_K_Flip_Flop j_k_ff_3 (
    .J(Count), .clk(not_3_out), .K(Count), .Q(j_k_ff_3_q), .reset(Clear));  // open: Qn, preset, en
  not not_4 (not_4_out, j_k_ff_3_q);
  assign Output[2] = Enable ? j_k_ff_3_q : 1'bz;  // Controlled_Buffer controlled_buffer_3
  J_K_Flip_Flop j_k_ff_4 (
    .J(Count), .clk(not_4_out), .K(Count), .Q(j_k_ff_4_q), .reset(Clear));  // open: Qn, preset, en
  assign Output[3] = Enable ? j_k_ff_4_q : 1'bz;  // Controlled_Buffer controlled_buffer_4

  // Notes on the sheet:
  //   1607073
endmodule

module ALU (
  input  [7:0] A,
  input  [7:0] B,
  input  Su,
  input  Eu,
  output [7:0] Output
);

  wire full_adder_1_cout, full_adder_2_cout, full_adder_3_cout, full_adder_4_cout, full_adder_5_cout,
       full_adder_6_cout, full_adder_7_cout;
  wire [7:0] Bit_Extender_out_2, full_adder_1_sum, xor_1_out;

  bit_extender Bit_Extender (.in_1(Su), .out_2(Bit_Extender_out_2));
  assign xor_1_out = B ^ Bit_Extender_out_2;  // XOR_Gate xor_1, 8 bits wide
  FULL_ADDER full_adder_1 (.Ai(A[0]), .Bi(xor_1_out[0]), .Cin(Su), .Sum(full_adder_1_sum[0]), .Cout(full_adder_1_cout));
  FULL_ADDER full_adder_2 (
    .Ai(A[1]), .Bi(xor_1_out[1]), .Cin(full_adder_1_cout), .Sum(full_adder_1_sum[1]), .Cout(full_adder_2_cout));
  FULL_ADDER full_adder_3 (
    .Ai(A[2]), .Bi(xor_1_out[2]), .Cin(full_adder_2_cout), .Sum(full_adder_1_sum[2]), .Cout(full_adder_3_cout));
  FULL_ADDER full_adder_4 (
    .Ai(A[3]), .Bi(xor_1_out[3]), .Cin(full_adder_3_cout), .Sum(full_adder_1_sum[3]), .Cout(full_adder_4_cout));
  FULL_ADDER full_adder_5 (
    .Ai(A[4]), .Bi(xor_1_out[4]), .Cin(full_adder_4_cout), .Sum(full_adder_1_sum[4]), .Cout(full_adder_5_cout));
  FULL_ADDER full_adder_6 (
    .Ai(A[5]), .Bi(xor_1_out[5]), .Cin(full_adder_5_cout), .Sum(full_adder_1_sum[5]), .Cout(full_adder_6_cout));
  FULL_ADDER full_adder_7 (
    .Ai(A[6]), .Bi(xor_1_out[6]), .Cin(full_adder_6_cout), .Sum(full_adder_1_sum[6]), .Cout(full_adder_7_cout));
  FULL_ADDER full_adder_8 (
    .Ai(A[7]), .Bi(xor_1_out[7]), .Cin(full_adder_7_cout), .Sum(full_adder_1_sum[7]));  // open: Cout
  assign Output = Eu ? full_adder_1_sum : 8'bz;  // Controlled_Buffer controlled_buffer_1

  // Notes on the sheet:
  //   Adder/Subtractor
  //   1607073
endmodule

module FULL_ADDER (
  input  Ai,
  input  Bi,
  input  Cin,
  output Sum,
  output Cout
);

  wire and_1_out, and_2_out, xor_1_out;

  xor xor_1 (xor_1_out, Ai, Bi);
  xor xor_2 (Sum, xor_1_out, Cin);
  and and_1 (and_1_out, Cin, xor_1_out);
  and and_2 (and_2_out, Bi, Ai);
  or or_1 (Cout, and_1_out, and_2_out);

  // Notes on the sheet:
  //   1607073
endmodule

module REGISTER_8_BIT (
  input  [7:0] Input,
  input  Load,
  input  clock_pulse,
  input  Clear,
  output [7:0] Output
);

  wire and_1_out, and_2_out, and_3_out, and_4_out, and_5_out, and_6_out, and_7_out, and_8_out, and_9_out,
       and_10_out, and_11_out, and_12_out, and_13_out, and_14_out, and_15_out, and_16_out, d_ff_1_q,
       d_ff_2_q, d_ff_3_q, d_ff_4_q, d_ff_5_q, d_ff_6_q, d_ff_7_q, d_ff_8_q, not_1_out, or_1_out, or_2_out,
       or_3_out, or_4_out, or_5_out, or_6_out, or_7_out, or_8_out;

  and and_1 (and_1_out, d_ff_1_q, not_1_out);
  assign Output[7] = 1'b1 ? d_ff_1_q : 1'bz;  // Controlled_Buffer controlled_buffer_1
  and and_2 (and_2_out, Input[7], Load);
  or or_1 (or_1_out, and_1_out, and_2_out);
  D_Flip_Flop d_ff_1 (.clk(clock_pulse), .D(or_1_out), .Q(d_ff_1_q), .reset(Clear));  // open: Qn, preset, en
  and and_3 (and_3_out, d_ff_2_q, not_1_out);
  assign Output[6] = 1'b1 ? d_ff_2_q : 1'bz;  // Controlled_Buffer controlled_buffer_2
  and and_4 (and_4_out, Input[6], Load);
  or or_2 (or_2_out, and_3_out, and_4_out);
  D_Flip_Flop d_ff_2 (.clk(clock_pulse), .D(or_2_out), .Q(d_ff_2_q), .reset(Clear));  // open: Qn, preset, en
  and and_5 (and_5_out, d_ff_3_q, not_1_out);
  assign Output[5] = 1'b1 ? d_ff_3_q : 1'bz;  // Controlled_Buffer controlled_buffer_3
  and and_6 (and_6_out, Input[5], Load);
  or or_3 (or_3_out, and_5_out, and_6_out);
  D_Flip_Flop d_ff_3 (.clk(clock_pulse), .D(or_3_out), .Q(d_ff_3_q), .reset(Clear));  // open: Qn, preset, en
  and and_7 (and_7_out, d_ff_4_q, not_1_out);
  assign Output[4] = 1'b1 ? d_ff_4_q : 1'bz;  // Controlled_Buffer controlled_buffer_4
  and and_8 (and_8_out, Input[4], Load);
  or or_4 (or_4_out, and_7_out, and_8_out);
  D_Flip_Flop d_ff_4 (.clk(clock_pulse), .D(or_4_out), .Q(d_ff_4_q), .reset(Clear));  // open: Qn, preset, en
  and and_9 (and_9_out, d_ff_5_q, not_1_out);
  assign Output[3] = 1'b1 ? d_ff_5_q : 1'bz;  // Controlled_Buffer controlled_buffer_5
  or or_5 (or_5_out, and_9_out, and_10_out);
  D_Flip_Flop d_ff_5 (.clk(clock_pulse), .D(or_5_out), .Q(d_ff_5_q), .reset(Clear));  // open: Qn, preset, en
  and and_10 (and_10_out, Input[3], Load);
  and and_11 (and_11_out, d_ff_6_q, not_1_out);
  assign Output[2] = 1'b1 ? d_ff_6_q : 1'bz;  // Controlled_Buffer controlled_buffer_6
  or or_6 (or_6_out, and_11_out, and_12_out);
  and and_12 (and_12_out, Input[2], Load);
  D_Flip_Flop d_ff_6 (.clk(clock_pulse), .D(or_6_out), .Q(d_ff_6_q), .reset(Clear));  // open: Qn, preset, en
  and and_13 (and_13_out, d_ff_7_q, not_1_out);
  assign Output[1] = 1'b1 ? d_ff_7_q : 1'bz;  // Controlled_Buffer controlled_buffer_7
  or or_7 (or_7_out, and_13_out, and_14_out);
  and and_14 (and_14_out, Input[1], Load);
  D_Flip_Flop d_ff_7 (.clk(clock_pulse), .D(or_7_out), .Q(d_ff_7_q), .reset(Clear));  // open: Qn, preset, en
  and and_15 (and_15_out, d_ff_8_q, not_1_out);
  assign Output[0] = 1'b1 ? d_ff_8_q : 1'bz;  // Controlled_Buffer controlled_buffer_8
  or or_8 (or_8_out, and_15_out, and_16_out);
  not not_1 (not_1_out, Load);
  and and_16 (and_16_out, Input[0], Load);
  D_Flip_Flop d_ff_8 (.clk(clock_pulse), .D(or_8_out), .Q(d_ff_8_q), .reset(Clear));  // open: Qn, preset, en

  // Notes on the sheet:
  //   1607073
endmodule

module Instruc_decoder (
  input  I7,
  input  I6,
  input  I5,
  input  I4,
  output LDA,
  output ADD,
  output SUB,
  output OUT,
  output HLT
);

  wire and_1_out, and_2_out, and_3_out, and_4_out, and_5_out, not_1_out, not_2_out, not_3_out, not_4_out;

  not not_1 (not_1_out, I7);
  not not_2 (not_2_out, I5);
  not not_3 (not_3_out, I6);
  not not_4 (not_4_out, I4);
  and and_1 (and_1_out, not_4_out, not_2_out, not_3_out, not_1_out);
  and and_2 (and_2_out, I4, not_2_out, not_3_out, not_1_out);
  and and_3 (and_3_out, not_4_out, I5, not_3_out, not_1_out);
  and and_4 (and_4_out, not_4_out, I5, I6, I7);
  and and_5 (and_5_out, I4, I5, I6, I7);
  buf buffer_1 (LDA, and_1_out);
  buf buffer_2 (ADD, and_2_out);
  buf buffer_3 (SUB, and_3_out);
  buf buffer_4 (OUT, and_4_out);
  buf buffer_5 (HLT, and_5_out);

  // Notes on the sheet:
  //   1607077
endmodule

module ring_counter (
  input  CLK,
  input  clear,
  output T6,
  output T5,
  output T4,
  output T3,
  output T2,
  output T1
);

  wire j_k_ff_1_qn, j_k_ff_2_qn, j_k_ff_3_qn, j_k_ff_4_qn, j_k_ff_5_qn, j_k_ff_6_q;

  J_K_Flip_Flop j_k_ff_1 (
    .J(T5), .clk(CLK), .K(j_k_ff_2_qn), .Q(T6), .Qn(j_k_ff_1_qn), .reset(clear));  // open: preset, en
  J_K_Flip_Flop j_k_ff_2 (
    .J(T4), .clk(CLK), .K(j_k_ff_3_qn), .Q(T5), .Qn(j_k_ff_2_qn), .reset(clear));  // open: preset, en
  J_K_Flip_Flop j_k_ff_3 (
    .J(T3), .clk(CLK), .K(j_k_ff_4_qn), .Q(T4), .Qn(j_k_ff_3_qn), .reset(clear));  // open: preset, en
  J_K_Flip_Flop j_k_ff_4 (
    .J(T2), .clk(CLK), .K(j_k_ff_5_qn), .Q(T3), .Qn(j_k_ff_4_qn), .reset(clear));  // open: preset, en
  J_K_Flip_Flop j_k_ff_5 (
    .J(T1), .clk(CLK), .K(j_k_ff_6_q), .Q(T2), .Qn(j_k_ff_5_qn), .reset(clear));  // open: preset, en
  J_K_Flip_Flop j_k_ff_6 (
    .J(j_k_ff_1_qn), .clk(CLK), .K(T6), .Q(j_k_ff_6_q), .Qn(T1), .reset(clear));  // open: preset, en

  // Notes on the sheet:
  //   Ring Counter
  //   1607077
endmodule

// Control sequencer
module controller (
  input  clear,
  input  CLK,
  input  I4,
  input  I5,
  input  I6,
  input  I7,
  output CP,
  output EP,
  output HLT,
  output nLM,
  output nCE,
  output nEI,
  output nLA,
  output EA,
  output SU,
  output EU,
  output nLB,
  output nLO,
  output nLI
);

  wire c39_1_out_7, c39_1_out_8, c39_1_out_9, c39_1_out_10, c40_1_out_7, c40_1_out_8, c40_1_out_9,
       c40_1_out_10, c41_1_out_8, c41_1_out_9, c41_1_out_10, c41_1_out_11, c42_1_out_10, c42_1_out_11,
       c43_1_out_6, c43_1_out_7, c43_1_out_8, counter_t3, counter_t4, counter_t5, counter_t6,
       Instruction_decoder_add, Instruction_decoder_lda, Instruction_decoder_out, Instruction_decoder_sub,
       not_2_out, or_1_out, or_2_out, or_3_out, or_4_out, or_6_out;

  Instruc_decoder Instruction_decoder (
    .I7(I7), .I6(I6), .I5(I5), .I4(I4), .LDA(Instruction_decoder_lda), .ADD(Instruction_decoder_add),
    .SUB(Instruction_decoder_sub), .OUT(Instruction_decoder_out), .HLT(HLT));
  C39 c39_1 (
    ._1(Instruction_decoder_lda), ._4(Instruction_decoder_add), ._9(Instruction_decoder_sub),
    ._10(counter_t4), ._12(Instruction_decoder_lda), ._13(counter_t5), .out_7(c39_1_out_7),
    .out_8(c39_1_out_8), .out_9(c39_1_out_9), .out_10(c39_1_out_10));
  or or_1 (or_1_out, EP, c39_1_out_7, c39_1_out_8, c39_1_out_9);
  not not_1 (nLM, or_1_out);
  not not_2 (not_2_out, CLK);
  C40 c40_1 (
    .in_1(Instruction_decoder_add), .in_2(Instruction_decoder_sub), .in_3(counter_t5),
    .in_4(Instruction_decoder_lda), .in_5(Instruction_decoder_add), .in_6(counter_t4), .out_7(c40_1_out_7),
    .out_8(c40_1_out_8), .out_9(c40_1_out_9), .out_10(c40_1_out_10));
  or or_2 (or_2_out, counter_t3, c39_1_out_10, c40_1_out_7, c40_1_out_8);
  not not_3 (nCE, or_2_out);
  ring_counter counter (
    .T6(counter_t6), .T5(counter_t5), .T4(counter_t4), .T3(counter_t3), .T2(CP), .T1(EP), .CLK(not_2_out),
    .clear(clear));
  or or_3 (or_3_out, c40_1_out_9, c40_1_out_10, c41_1_out_8);
  not not_4 (nEI, or_3_out);
  C41 c41_1 (
    .in_5(Instruction_decoder_sub), .in_6(counter_t4), .in_1(Instruction_decoder_lda), .in_2(counter_t5),
    .in_7(Instruction_decoder_add), .in_3(Instruction_decoder_sub), .in_4(counter_t6), .out_8(c41_1_out_8),
    .out_9(c41_1_out_9), .out_10(c41_1_out_10), .out_11(c41_1_out_11));
  or or_4 (or_4_out, c41_1_out_9, c41_1_out_10, c41_1_out_11);
  not not_5 (nLA, or_4_out);
  C42 c42_1 (
    .in_5(Instruction_decoder_out), .in_6(counter_t4), .in_1(Instruction_decoder_sub), .in_2(counter_t6),
    .in_7(Instruction_decoder_add), .in_3(Instruction_decoder_sub), .in_4(counter_t6), .out_8(EA),
    .out_9(SU), .out_10(c42_1_out_10), .out_11(c42_1_out_11));
  or or_5 (EU, c42_1_out_10, c42_1_out_11);
  C43 c43_1 (
    .in_1(Instruction_decoder_add), .in_2(Instruction_decoder_sub), .in_3(counter_t5),
    .in_4(Instruction_decoder_out), .in_5(counter_t4), .out_6(c43_1_out_6), .out_7(c43_1_out_7),
    .out_8(c43_1_out_8));
  or or_6 (or_6_out, c43_1_out_6, c43_1_out_7);
  not not_6 (nLB, or_6_out);
  not not_7 (nLO, c43_1_out_8);
  not not_8 (nLI, counter_t3);

  // Notes on the sheet:
  //   1607077
endmodule

module C39 (
  input  _1,
  input  _4,
  input  _9,
  input  _10,
  input  _13,
  input  _12,
  output out_7,
  output out_8,
  output out_9,
  output out_10
);

  and and_1 (out_7, _1, _10);
  and and_2 (out_8, _4, _10);
  and and_3 (out_9, _9, _10);
  and and_4 (out_10, _12, _13);
endmodule

module C40 (
  input  in_1,
  input  in_2,
  input  in_3,
  input  in_4,
  input  in_5,
  input  in_6,
  output out_7,
  output out_8,
  output out_9,
  output out_10
);

  and and_1 (out_8, in_2, in_3);
  and and_2 (out_7, in_1, in_3);
  and and_3 (out_9, in_4, in_6);
  and and_4 (out_10, in_5, in_6);
endmodule

module C41 (
  input  in_1,
  input  in_2,
  input  in_3,
  input  in_4,
  input  in_5,
  input  in_6,
  input  in_7,
  output out_8,
  output out_9,
  output out_10,
  output out_11
);

  and and_1 (out_9, in_1, in_2);
  and and_2 (out_8, in_5, in_6);
  and and_3 (out_10, in_7, in_4);
  and and_4 (out_11, in_3, in_4);
endmodule

module C43 (
  input  in_1,
  input  in_2,
  input  in_3,
  input  in_4,
  input  in_5,
  output out_6,
  output out_7,
  output out_8
);

  and and_1 (out_7, in_2, in_3);
  and and_2 (out_6, in_1, in_3);
  and and_3 (out_8, in_4, in_5);
endmodule

module C42 (
  input  in_1,
  input  in_2,
  input  in_3,
  input  in_4,
  input  in_5,
  input  in_6,
  input  in_7,
  output out_8,
  output out_9,
  output out_10,
  output out_11
);

  and and_1 (out_8, in_5, in_6);
  and and_2 (out_9, in_1, in_2);
  and and_3 (out_10, in_7, in_4);
  and and_4 (out_11, in_3, in_4);
endmodule

module bit_extender (
  input  in_1,
  output [7:0] out_2
);


  assign out_2 = {8{in_1}};

  // Notes on the sheet:
  //   1607073
endmodule
